# Fritzing sketch ReprapController (saved by Fritzing 0.9.0b)

parts:
  J2 = male pin header, 11 pins [form="♂ (male)"]
  OLED1 = 128x32 I2C Monochrome OLED Display
  SdModule1 = SdModule
  ENCODER1 = Rotary Encoder with Knob
  J11 = male pin header, 4 pins [form="♂ (male)"]  # not connected
  J12 = male pin header, 3 pins [form="♂ (male)"]  # not connected
  J13 = male pin header, 3 pins [form="♂ (male)"]  # not connected
  J16 = male pin header, 5 pins [form="♂ (male)"]
  J17 = male pin header, 5 pins [form="♂ (male)"]  # not connected
  J18 = male pin header, 4 pins [form="♂ (male)"]  # not connected
  J19 = male pin header, 4 pins [form="♂ (male)"]  # not connected
  J20 = Piezo Speaker

nets:
  N1: J2.pin1, OLED1.SCL
  N2: J2.pin2, OLED1.SDA
  GND: J2.pin3, OLED1.GND, SdModule1.GND, ENCODER1.no_name_yet#2, ENCODER1.no_name_yet#5, J20.pin1
  VIN: J2.pin4, OLED1.VIN, SdModule1.5V
  N3: J2.pin5, SdModule1.SS
  N4: J2.pin6, SdModule1.SCK
  N5: J2.pin7, SdModule1.MISO
  N6: J2.pin8, SdModule1.MOSI
  N7: J2.pin9, ENCODER1.no_name_yet#4
  N8: J2.pin10, ENCODER1.no_name_yet#1
  N9: J2.pin11, ENCODER1.no_name_yet#3
  N10: J16.pin5, J20.pin2

notes:
  SCL
  SDA
  GND
  5V
  SD CS
  SD SCK
  SD MOSI
  SD MISO
  ENC Button
  ENC A
  ENC B
  I2C
  VCC
  Reset
  MISO (D50)
  ICSP
  SCK (D52)
  MOSI (D51)
  A5
  A7
  A9
  A12
  D42
  D43
  D17 (RX2)
  A11
  Aux2 / Keypad
  D46
  D48
  D49
  AUX3
  D47

custom parts:
  Rotary Encoder with Knob: Rotary Encoder with 1/4" Shaft and Knob
